# Fritzing sketch Current sensor (saved by Fritzing 0.9.3b)
breadboards: 1

parts:
  Part1 = Arduino Mega 2560 (Rev3)
  U2 = 74HC4067 [package=ssop24]
  Part2 = ACS712 Low Current Sensor Board v12
  Part3 = ACS712 Low Current Sensor Board v12

nets:
  N1: Part1.A8, U2.COM
  GND: Part1.GND, U2.GND, U2.EN
  5V: Part1.5V, U2.VCC
  N2: Part1.D25, U2.S0
  N3: Part1.D26, U2.S1
  N4: Part1.D27, U2.S2
  N5: Part1.D28, U2.S3
  N6: U2.CHAN0, Part2.VO
  N7: U2.CHAN8, Part3.VO
