# Fritzing sketch Temperature sensor (saved by Fritzing 0.9.3b)
breadboards: 1

parts:
  Part1 = Arduino Mega 2560 (Rev3)
  U2 = 74HC4067 [package=ssop24]
  T1 = LM35 Temperature Sensor [package="TO92 [THT]"]
  T2 = LM35 Temperature Sensor [package="TO92 [THT]"]
  BAT1 = Battery Holders [package=battery-aa]
  BAT2 = Battery Holders [package=battery-aa]

nets:
  N1: Part1.A13, U2.COM
  GND: Part1.GND, U2.GND, U2.EN, T1.GND, T2.GND
  5V: Part1.5V, U2.VCC
  N2: Part1.D25, U2.S0
  N3: Part1.D26, U2.S1
  N4: Part1.D27, U2.S2
  N5: Part1.D28, U2.S3
  N6: U2.CHAN0, T1.Vout
  N7: U2.CHAN8, T2.Vout
  N8: T1.+Vs, BAT2.+
  N9: T2.+Vs, BAT1.+
  N10: BAT1.-, BAT2.-
